# Fritzing sketch DMX_to_IR (saved by Fritzing 0.9.1b)
circuit board: 8.46667cm x 5.64444cm
breadboards: 1

parts:
  Part1 = Arduino Nano (Rev3.0)
  R2 = Resistor [tolerance=±5% resistance=100 package=THT]
  XLR1 = XLR3_NCFAH2 [package=xlr3_nc3fah2]
  R1 = Resistor [tolerance=±5% resistance=2.2k package=THT]
  RJ11_Female1 = RJ11 Jack [package=rj11-6]
  RJ11_Male = RJ11 Jack [package=rj11-6]
  R4 = Resistor [tolerance=±5% resistance=100 part_number=Termination package=THT]
  RJ11_Female = RJ11 Jack [package=rj11-6]
  R3 = Resistor [tolerance=±5% resistance=100 part_number=Terminator package=THT]
  Close_for_DMX_open_for_Flash = Solder Jumper [part_number="Jumper 1" package=sj_2s-trace]
  IR_LED = LEDs [package=led10mm]
  BC337_(max_800mA) = NPN-Transistor [package="TO92 [THT]"]
  U1 = MAX485 [package=dil08]

nets:
  N1: Part1.D1/TX, U1.DI
  N2: Part1.D0/RX, Close_for_DMX_open_for_Flash.1
  GND: Part1.GND, XLR1.1, XLR1.G, R4.Pin_1, R3.Pin_1, BC337_(max_800mA).E, U1.GND
  N3: Part1.D3, R1.Pin_0
  N4: Part1.D6, U1.RE, U1.DE
  9V: Part1.VIN, RJ11_Female1.6, RJ11_Female.6
  5V: Part1.5V, U1.VCC
  N5: R2.Pin_0, RJ11_Male.6
  N6: R2.Pin_1, IR_LED.A
  N7: XLR1.2, R4.Pin_0, U1.B
  N8: XLR1.3, R3.Pin_0, U1.A
  N9: R1.Pin_1, BC337_(max_800mA).B
  N10: RJ11_Female1.1, RJ11_Female.1, BC337_(max_800mA).C
  N11: RJ11_Male.1, IR_LED.C
  N12: Close_for_DMX_open_for_Flash.2, U1.RO

notes:
  close for normal operation, open for programming
  github.com/timmo/Arduino_DMX_to_IR
